# Fritzing sketch microsd-storage-nrf52840 (saved by Fritzing 1.0.8)
breadboards: 2

parts:
  Part1 = NRF52840 Pro Micro
  µSD1 = microSD Card Module
  OLED_I2C1 = OLED 128x64 I2C Monochrome Display

nets:
  N1: Part1.104, µSD1.CS
  N2: Part1.011, OLED_I2C1.SCK
  N3: Part1.100, OLED_I2C1.SDA
  N4: Part1.022, µSD1.MOSI
  N5: Part1.020, µSD1.MISO
  N6: Part1.017, µSD1.CLK
  GND: Part1.GND, Part1.B-, µSD1.GND, OLED_I2C1.GND
  VCC: Part1.VCC, µSD1.3.3V, OLED_I2C1.VDD

custom parts:
  NRF52840 Pro Micro: Pro Micro nRF52840 boards are Arduino Pro Micro-compatible development boards based on the nRF52840 SoC. This is a generic board definition that supports multiple variants with compatible pinouts. There are many variants available, including: Compatible: Nice!Nano V2 (official, open-source) SuperMini nRF52840 ProMicro nRF52840 Mikoto 52840nano (more GPIO) Similar: nRFMicro BlueMicro All these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
  microSD Card Module: microSD Card Reader This is a simple, generic, 3.3V only SD card reader module. It does not include any regulator or logic level shifting circuitry.
