# Fritzing sketch poc-piezo-sensor-nrf52840 (saved by Fritzing 1.0.8)
breadboards: 1

parts:
  Part1 = NRF52840 Pro Micro
  Part2 = InvenSense MPU6050
  OLED_I2C1 = OLED 128x64 I2C Monochrome Display
  A2 = PWM Vibration Motor Switch Toy Sensor Module/Mobile Phone Vibrator (DC 5V)
  R2 = Resistor [tolerance=±5% power=0.25W resistance=10k package=THT]
  J1 = Piezo Speaker
  R3 = Resistor [tolerance=±5% power=0.25W resistance=10k package=THT]

nets:
  N1: Part1.011, Part2.SCL, OLED_I2C1.SCK
  N2: Part1.100, Part2.SDA, OLED_I2C1.SDA
  N3: Part1.024, Part2.INT
  GND: Part1.GND, Part1.B-, Part2.GND, OLED_I2C1.GND, A2.GND, R2.Pin_1, J1.pin1, R3.Pin_0
  N4: Part1.009, A2.IN, R2.Pin_0
  N5: Part1.002, R3.Pin_1
  VCC: Part1.VCC, Part2.VCC, OLED_I2C1.VDD, A2.VCC

custom parts:
  NRF52840 Pro Micro: Pro Micro nRF52840 boards are Arduino Pro Micro-compatible development boards based on the nRF52840 SoC. This is a generic board definition that supports multiple variants with compatible pinouts. There are many variants available, including: Compatible: Nice!Nano V2 (official, open-source) SuperMini nRF52840 ProMicro nRF52840 Mikoto 52840nano (more GPIO) Similar: nRFMicro BlueMicro All these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
