# Fritzing sketch ui-mpu-6050-with-oled-on-nrf52840 (saved by Fritzing 1.0.8)
breadboards: 1

parts:
  Part2 = InvenSense MPU6050
  S1 = Momentary Switch [package=tactile-pth]
  OLED_I2C1 = OLED 128x64 I2C Monochrome Display
  Part1 = NRF52840 Pro Micro

nets:
  VCC: Part2.VCC, OLED_I2C1.VDD, Part1.VCC
  GND: Part2.GND, S1.3, OLED_I2C1.GND, Part1.GND, Part1.B-
  N1: Part2.SCL, OLED_I2C1.SCK, Part1.011
  N2: Part2.SDA, OLED_I2C1.SDA, Part1.100
  N3: S1.4, Part1.RST

custom parts:
  NRF52840 Pro Micro: Pro Micro nRF52840 boards are Arduino Pro Micro-compatible development boards based on the nRF52840 SoC. This is a generic board definition that supports multiple variants with compatible pinouts. There are many variants available, including: Compatible: Nice!Nano V2 (official, open-source) SuperMini nRF52840 ProMicro nRF52840 Mikoto 52840nano (more GPIO) Similar: nRFMicro BlueMicro All these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
